# Fritzing sketch MeteoEstacionLoRa_bb (saved by Fritzing 0.9.10b)
breadboards: 1

parts:
  M3 = Adafruit Anemometer [package=THT]
  Mod4 = Heltec CubeCell Dev-Board [part_number=HTCC-AB01]
  Solar_Panel1 = Solar Cell
  U2 = Battery Holders [package=lipo-1100mAh]  # not connected
  R1 = Resistor [tolerance=±5% resistance=10k package="2512 [SMD]"]
  DHT2 = DHT22 Humidity and Temperature Sensor

nets:
  N1: M3.pin1, Mod4.pin_16, DHT2.VDD
  N2: M3.pin2, Mod4.pin_21
  N3: Mod4.pin4, DHT2.DATA
  N4: Mod4.pin_11, Mod4.pin_14, Mod4.pin_18, Solar_Panel1.-, R1.Pin_0, DHT2.GND
  N5: Mod4.pin_15, Solar_Panel1.+

custom parts:
  Adafruit Anemometer: Adafruit Anemometer Wind Speed Sensor w/Analog Voltage Output.
  Heltec CubeCell Dev-Board: CubeCell is a part of the Heltec LoRa series and incorporates a PSoC 4000 series processor and SX1262 RF transceiver with an integrated CP2102 USB to serial port interface and onboard SHT1.25 battery interface with integrated lithium battery management system, supporting direct solar panel connection. Links: Heltec CubeCell Dev-Board product page Github
